// Logisim project harjoitus2.circ as structural Verilog
module h2_1a (
  input  A,
  input  B,
  input  C,
  input  D,
  output E,
  output F,
  output G,
  output H
);

  wire and_1_out, and_2_out, and_3_out, and_4_out, and_5_out, and_6_out, and_7_out, and_8_out, and_9_out,
       not_1_out, not_2_out, not_3_out, not_4_out, not_5_out, not_6_out, not_7_out, not_8_out, not_9_out,
       not_10_out, not_11_out, not_12_out;

  not not_1 (not_1_out, A);
  not not_2 (not_2_out, A);
  not not_3 (not_3_out, A);
  not not_4 (not_4_out, B);
  not not_5 (not_5_out, C);
  not not_6 (not_6_out, D);
  not not_7 (not_7_out, B);
  and and_1 (and_1_out, not_7_out, D);
  not not_8 (not_8_out, B);
  and and_2 (and_2_out, not_8_out, C);
  and and_3 (and_3_out, B, not_9_out, not_10_out);
  not not_9 (not_9_out, C);
  not not_10 (not_10_out, D);
  not not_11 (not_11_out, C);
  and and_4 (and_4_out, not_11_out, D);
  and and_5 (and_5_out, C, not_12_out);
  not not_12 (not_12_out, D);
  and and_6 (and_6_out, not_1_out, D);
  and and_7 (and_7_out, not_2_out, C);
  and and_8 (and_8_out, not_3_out, B);
  and and_9 (and_9_out, A, not_4_out, not_5_out, not_6_out);
  or or_1 (F, and_1_out, and_2_out, and_3_out);
  or or_2 (G, and_4_out, and_5_out);
  or or_3 (E, and_6_out, and_7_out, and_8_out, and_9_out);

  assign H = D;
endmodule

module h2_2a (
  input  A,
  input  B,
  input  C,
  input  D,
  output f12,
  output f11,
  output f10,
  output f9,
  output f8,
  output f7,
  output f6,
  output f5,
  output f4,
  output f3,
  output f2,
  output f1
);

  wire and_3_out, and_4_out, and_5_out, and_6_out, and_7_out, and_8_out, and_9_out, and_10_out, and_11_out,
       and_12_out;

  and and_1 (f12, A, B, C);
  and and_2 (f11, A, B);
  and and_3 (and_3_out, A, C);
  and and_4 (and_4_out, A, B);
  and and_5 (and_5_out, A, D);
  and and_6 (and_6_out, A, C);
  and and_7 (and_7_out, A, B);
  and and_8 (and_8_out, B, C, D);
  and and_9 (and_9_out, B, C);
  and and_10 (and_10_out, B, D);
  and and_11 (and_11_out, B, C);
  or or_1 (f4, B, A);
  and and_12 (and_12_out, C, D);
  or or_2 (f2, C, B, A);
  or or_3 (f1, D, C, B, A);
  or or_4 (f10, and_3_out, and_4_out);
  or or_5 (f9, and_5_out, and_6_out, and_7_out);
  or or_6 (f7, and_8_out, A);
  or or_7 (f6, and_9_out, A);
  or or_8 (f5, and_10_out, and_11_out, A);
  or or_9 (f3, and_12_out, B, A);

  assign f8 = A;
endmodule

module h2_2b (
);

  wire h2_2a_1_f2, h2_2a_1_f3, h2_2a_1_f4, h2_2a_1_f5, h2_2a_1_f6, h2_2a_1_f7, h2_2a_1_f8, h2_2a_1_f9,
       h2_2a_1_f10, h2_2a_1_f11, h2_2a_1_f12, music_1_p2;
  wire [3:0] music_1_p1;

  // Probe on music_1_p1
  // Music music_1: pin names not known; wires that end beside it: music_1_p1, music_1_p2
  h2_2a h2_2a_1 (
    .A(music_1_p1[3]), .B(music_1_p1[2]), .C(music_1_p1[1]), .D(music_1_p1[0]), .f12(h2_2a_1_f12),
    .f11(h2_2a_1_f11), .f10(h2_2a_1_f10), .f9(h2_2a_1_f9), .f8(h2_2a_1_f8), .f7(h2_2a_1_f7), .f6(h2_2a_1_f6),
    .f5(h2_2a_1_f5), .f4(h2_2a_1_f4), .f3(h2_2a_1_f3), .f2(h2_2a_1_f2), .f1(music_1_p2));
  LED led_1 (.in(h2_2a_1_f12));
  LED led_2 (.in(h2_2a_1_f11));
  LED led_3 (.in(h2_2a_1_f10));
  LED led_4 (.in(h2_2a_1_f9));
  LED led_5 (.in(h2_2a_1_f8));
  LED led_6 (.in(h2_2a_1_f7));
  LED led_7 (.in(h2_2a_1_f6));
  LED led_8 (.in(h2_2a_1_f5));
  LED led_9 (.in(h2_2a_1_f4));
  LED led_10 (.in(h2_2a_1_f3));
  LED led_11 (.in(h2_2a_1_f2));
  LED led_12 (.in(music_1_p2));
endmodule

module h2_3a (
  input  A,
  input  B,
  output E
);

  wire and_1_out, and_2_out, not_1_out, not_2_out;

  not not_1 (not_1_out, A);
  not not_2 (not_2_out, B);
  and and_1 (and_1_out, not_1_out, B);
  and and_2 (and_2_out, A, not_2_out);
  or or_1 (E, and_1_out, and_2_out);
endmodule

module h2_3b (
  input  A,
  input  B,
  output E
);

  wire not_1_out, not_2_out;

  not not_1 (not_1_out, A);
  not not_2 (not_2_out, B);
  or or_1 (E, not_1_out, not_2_out);
endmodule

module h2_3c (
  input  B,
  input  A,
  output out_3
);

  wire n7400_1_p3, n7400_1_p5, n7400_1_p10, n7400_1_p12;

  // _7400 7400_1: pin names not known; wires that end beside it: B, B, n7400_1_p3, n7400_1_p3, n7400_1_p5, 1'b0, 1'b1, A, A, n7400_1_p10, n7400_1_p10, n7400_1_p12
  // _7400 7400_2: pin names not known; wires that end beside it: n7400_1_p12, n7400_1_p5, out_3, 1'b0, 1'b1
endmodule

module h2_1b (
);

  wire button_1_out;
  wire [3:0] adder_1_out, counter_1_q, h2_1a_1_h;

  Button button_1 (.out(button_1_out));
  Counter #(.width(4), .max('hf)) counter_1 (.Q(counter_1_q), .clk(button_1_out));  // open: load, D, count, carry, clr
  Adder #(.width(4)) adder_1 (.a(h2_1a_1_h), .b(counter_1_q), .out(adder_1_out));  // open: cin, cout
  h2_1a h2_1a_1 (
    .A(counter_1_q[3]), .B(counter_1_q[2]), .C(counter_1_q[1]), .D(counter_1_q[0]), .E(h2_1a_1_h[3]),
    .F(h2_1a_1_h[2]), .G(h2_1a_1_h[1]), .H(h2_1a_1_h[0]));
  // Probe on adder_1_out
endmodule
